// Logisim project 16-bit left shifter.circ as structural Verilog: 1 circuit, main circuit main
module main (
  input  _0,
  input  _1,
  input  _2,
  input  _3,
  input  _4,
  input  _5,
  input  _6,
  input  _7,
  input  _8,
  input  _9,
  input  _10,
  input  _11,
  input  _12,
  input  _13,
  input  _14,
  input  _15,
  input  in_17,
  output _0_2,
  output _1_2,
  output _2_2,
  output _3_2,
  output _4_2,
  output _5_2,
  output _6_2,
  output _7_2,
  output _8_2,
  output _9_2,
  output _10_2,
  output _11_2,
  output _12_2,
  output _13_2,
  output _14_2,
  output _15_2
);

  wire and_1_out, and_3_out, and_4_out, and_5_out, and_6_out, and_7_out, and_8_out, and_9_out, and_10_out,
       and_11_out, and_12_out, and_13_out, and_14_out, and_15_out, and_16_out, and_17_out, and_18_out,
       and_19_out, and_20_out, and_21_out, and_22_out, and_23_out, and_24_out, and_25_out, and_26_out,
       and_27_out, and_28_out, and_30_out, not_1_out;

  not not_1 (not_1_out, in_17);
  and and_1 (and_1_out, _0, in_17);
  and and_2 (_0_2, not_1_out, _1);
  and and_3 (and_3_out, _1, in_17);
  or or_1 (_1_2, and_1_out, and_4_out);
  and and_4 (and_4_out, not_1_out, _2);
  and and_5 (and_5_out, _2, in_17);
  or or_2 (_2_2, and_3_out, and_6_out);
  and and_6 (and_6_out, not_1_out, _3);
  and and_7 (and_7_out, _3, in_17);
  or or_3 (_3_2, and_5_out, and_8_out);
  and and_8 (and_8_out, not_1_out, _4);
  or or_4 (_4_2, and_7_out, and_9_out);
  and and_9 (and_9_out, not_1_out, _5);
  and and_10 (and_10_out, _4, in_17);
  and and_11 (and_11_out, _5, in_17);
  or or_5 (_5_2, and_10_out, and_12_out);
  and and_12 (and_12_out, not_1_out, _6);
  and and_13 (and_13_out, _6, in_17);
  or or_6 (_6_2, and_11_out, and_14_out);
  and and_14 (and_14_out, not_1_out, _7);
  and and_15 (and_15_out, _7, in_17);
  or or_7 (_7_2, and_13_out, and_16_out);
  and and_16 (and_16_out, not_1_out, _8);
  or or_8 (_8_2, and_15_out, and_17_out);
  and and_17 (and_17_out, not_1_out, _9);
  and and_18 (and_18_out, _8, in_17);
  and and_19 (and_19_out, _9, in_17);
  or or_9 (_9_2, and_18_out, and_20_out);
  and and_20 (and_20_out, not_1_out, _10);
  and and_21 (and_21_out, _10, in_17);
  or or_10 (_10_2, and_19_out, and_22_out);
  and and_22 (and_22_out, not_1_out, _11);
  and and_23 (and_23_out, _11, in_17);
  or or_11 (_11_2, and_21_out, and_24_out);
  and and_24 (and_24_out, not_1_out, _12);
  and and_25 (and_25_out, _12, in_17);
  or or_12 (_12_2, and_23_out, and_26_out);
  and and_26 (and_26_out, not_1_out, _13);
  or or_13 (_13_2, and_25_out, and_28_out);
  and and_27 (and_27_out, _13, in_17);
  and and_28 (and_28_out, not_1_out, _14);
  and and_29 (_15_2, _14, in_17);
  or or_14 (_14_2, and_27_out, and_30_out);
  and and_30 (and_30_out, not_1_out, _15);
endmodule
