// Logisim project 32bit ALU - CO, SelmaK.circ as structural Verilog: 10 circuits, main circuit main
module main (
  input  [2:0] Operation__opcode,
  input  [31:0] A_Input,
  input  EN,
  input  [31:0] B_Input,
  output [31:0] Output
);

  wire [31:0] addition_000_result, AND_010_result, LeftShift_A_111_result, NOT_A_101_result,
       NOT_B_110_result, OR_011_result, subtraction_001_result, XOR_100_result;

  addition addition_000 (.A(A_Input), .Result(addition_000_result), .B(B_Input));
  subtraction subtraction_001 (.A(A_Input), .B(B_Input), .Result(subtraction_001_result));
  bitwise_AND AND_010 (.A(A_Input), .B(B_Input), .Result(AND_010_result));
  bitwise_OR OR_011 (.A(A_Input), .B(B_Input), .Result(OR_011_result));
  Bitwise_XOR XOR_100 (.A(A_Input), .B(B_Input), .Result(XOR_100_result));
  Bitwise_not NOT_A_101 (.in_1(A_Input), .Result(NOT_A_101_result));
  Bitwise_not NOT_B_110 (.in_1(B_Input), .Result(NOT_B_110_result));
  left_shift LeftShift_A_111 (.A(A_Input), .Result(LeftShift_A_111_result));  // open: in_2
  Multiplexer #(.select(3), .width(32)) multiplexer_1 (
    .in0(addition_000_result), .in1(subtraction_001_result), .in2(AND_010_result), .in3(OR_011_result),
    .in4(XOR_100_result), .in5(NOT_A_101_result), .in6(NOT_B_110_result), .in7(LeftShift_A_111_result),
    .out(Output), .sel(Operation__opcode), .en(EN));
endmodule

module addition (
  input  [31:0] A,
  input  [31:0] B,
  output [31:0] Result
);

  wire full_adder_1_out_5, full_adder_2_out_5, full_adder_3_out_5, full_adder_4_out_5, full_adder_5_out_5,
       full_adder_6_out_5, full_adder_7_out_5, full_adder_8_out_5, full_adder_9_out_5, full_adder_10_out_5,
       full_adder_11_out_5, full_adder_12_out_5, full_adder_13_out_5, full_adder_14_out_5,
       full_adder_15_out_5, full_adder_16_out_5, full_adder_17_out_5, full_adder_18_out_5,
       full_adder_19_out_5, full_adder_20_out_5, full_adder_21_out_5, full_adder_22_out_5,
       full_adder_23_out_5, full_adder_24_out_5, full_adder_25_out_5, full_adder_26_out_5,
       full_adder_27_out_5, full_adder_28_out_5, full_adder_29_out_5, full_adder_30_out_5,
       full_adder_31_out_5;

  Full_Adder full_adder_1 (.in_1(A[24]), .in_2(B[24]), .in_3(1'b0), .out_4(Result[24]), .out_5(full_adder_1_out_5));
  Full_Adder full_adder_2 (
    .in_1(A[25]), .in_2(B[25]), .in_3(full_adder_1_out_5), .out_4(Result[25]), .out_5(full_adder_2_out_5));
  Full_Adder full_adder_3 (
    .in_1(A[26]), .in_2(B[26]), .in_3(full_adder_2_out_5), .out_4(Result[26]), .out_5(full_adder_3_out_5));
  Full_Adder full_adder_4 (
    .in_1(A[27]), .in_2(B[27]), .in_3(full_adder_3_out_5), .out_4(Result[27]), .out_5(full_adder_4_out_5));
  Full_Adder full_adder_5 (
    .in_1(A[28]), .in_2(B[28]), .in_3(full_adder_4_out_5), .out_4(Result[28]), .out_5(full_adder_5_out_5));
  Full_Adder full_adder_6 (
    .in_1(A[29]), .in_2(B[29]), .in_3(full_adder_5_out_5), .out_4(Result[29]), .out_5(full_adder_6_out_5));
  Full_Adder full_adder_7 (
    .in_1(A[30]), .in_2(B[30]), .in_3(full_adder_6_out_5), .out_4(Result[30]), .out_5(full_adder_7_out_5));
  Full_Adder full_adder_8 (
    .in_1(A[31]), .in_2(B[31]), .in_3(full_adder_7_out_5), .out_4(Result[31]), .out_5(full_adder_8_out_5));
  Full_Adder full_adder_9 (
    .in_1(A[16]), .in_2(B[16]), .in_3(full_adder_8_out_5), .out_4(Result[16]), .out_5(full_adder_9_out_5));
  Full_Adder full_adder_10 (
    .in_1(A[17]), .in_2(B[17]), .in_3(full_adder_9_out_5), .out_4(Result[17]), .out_5(full_adder_10_out_5));
  Full_Adder full_adder_11 (
    .in_1(A[18]), .in_2(B[18]), .in_3(full_adder_10_out_5), .out_4(Result[18]), .out_5(full_adder_11_out_5));
  Full_Adder full_adder_12 (
    .in_1(A[19]), .in_2(B[19]), .in_3(full_adder_11_out_5), .out_4(Result[19]), .out_5(full_adder_12_out_5));
  Full_Adder full_adder_13 (
    .in_1(A[20]), .in_2(B[20]), .in_3(full_adder_12_out_5), .out_4(Result[20]), .out_5(full_adder_13_out_5));
  Full_Adder full_adder_14 (
    .in_1(A[21]), .in_2(B[21]), .in_3(full_adder_13_out_5), .out_4(Result[21]), .out_5(full_adder_14_out_5));
  Full_Adder full_adder_15 (
    .in_1(A[22]), .in_2(B[22]), .in_3(full_adder_14_out_5), .out_4(Result[22]), .out_5(full_adder_15_out_5));
  Full_Adder full_adder_16 (
    .in_1(A[23]), .in_2(B[23]), .in_3(full_adder_15_out_5), .out_4(Result[23]), .out_5(full_adder_16_out_5));
  Full_Adder full_adder_17 (
    .in_1(A[8]), .in_2(B[8]), .in_3(full_adder_16_out_5), .out_4(Result[8]), .out_5(full_adder_17_out_5));
  Full_Adder full_adder_18 (
    .in_1(A[9]), .in_2(B[9]), .in_3(full_adder_17_out_5), .out_4(Result[9]), .out_5(full_adder_18_out_5));
  Full_Adder full_adder_19 (
    .in_1(A[10]), .in_2(B[10]), .in_3(full_adder_18_out_5), .out_4(Result[10]), .out_5(full_adder_19_out_5));
  Full_Adder full_adder_20 (
    .in_1(A[11]), .in_2(B[11]), .in_3(full_adder_19_out_5), .out_4(Result[11]), .out_5(full_adder_20_out_5));
  Full_Adder full_adder_21 (
    .in_1(A[12]), .in_2(B[12]), .in_3(full_adder_20_out_5), .out_4(Result[12]), .out_5(full_adder_21_out_5));
  Full_Adder full_adder_22 (
    .in_1(A[13]), .in_2(B[13]), .in_3(full_adder_21_out_5), .out_4(Result[13]), .out_5(full_adder_22_out_5));
  Full_Adder full_adder_23 (
    .in_1(A[14]), .in_2(B[14]), .in_3(full_adder_22_out_5), .out_4(Result[14]), .out_5(full_adder_23_out_5));
  Full_Adder full_adder_24 (
    .in_1(A[15]), .in_2(B[15]), .in_3(full_adder_23_out_5), .out_4(Result[15]), .out_5(full_adder_24_out_5));
  Full_Adder full_adder_25 (
    .in_1(A[0]), .in_2(B[0]), .in_3(full_adder_24_out_5), .out_4(Result[0]), .out_5(full_adder_25_out_5));
  Full_Adder full_adder_26 (
    .in_1(A[1]), .in_2(B[1]), .in_3(full_adder_25_out_5), .out_4(Result[1]), .out_5(full_adder_26_out_5));
  Full_Adder full_adder_27 (
    .in_1(A[2]), .in_2(B[2]), .in_3(full_adder_26_out_5), .out_4(Result[2]), .out_5(full_adder_27_out_5));
  Full_Adder full_adder_28 (
    .in_1(A[3]), .in_2(B[3]), .in_3(full_adder_27_out_5), .out_4(Result[3]), .out_5(full_adder_28_out_5));
  Full_Adder full_adder_29 (
    .in_1(A[4]), .in_2(B[4]), .in_3(full_adder_28_out_5), .out_4(Result[4]), .out_5(full_adder_29_out_5));
  Full_Adder full_adder_30 (
    .in_1(A[5]), .in_2(B[5]), .in_3(full_adder_29_out_5), .out_4(Result[5]), .out_5(full_adder_30_out_5));
  Full_Adder full_adder_31 (
    .in_1(A[6]), .in_2(B[6]), .in_3(full_adder_30_out_5), .out_4(Result[6]), .out_5(full_adder_31_out_5));
  Full_Adder full_adder_32 (.in_1(A[7]), .in_2(B[7]), .in_3(full_adder_31_out_5), .out_4(Result[7]));  // open: out_5
endmodule

module subtraction (
  input  [31:0] A,
  input  [31:0] B,
  output [31:0] Result
);

  wire full_subtractor_1_out_5, full_subtractor_2_out_5, full_subtractor_3_out_5, full_subtractor_4_out_5,
       full_subtractor_5_out_5, full_subtractor_6_out_5, full_subtractor_7_out_5, full_subtractor_8_out_5,
       full_subtractor_9_out_5, full_subtractor_10_out_5, full_subtractor_11_out_5, full_subtractor_12_out_5,
       full_subtractor_13_out_5, full_subtractor_14_out_5, full_subtractor_15_out_5,
       full_subtractor_16_out_5, full_subtractor_17_out_5, full_subtractor_18_out_5,
       full_subtractor_19_out_5, full_subtractor_20_out_5, full_subtractor_21_out_5,
       full_subtractor_22_out_5, full_subtractor_23_out_5, full_subtractor_24_out_5,
       full_subtractor_25_out_5, full_subtractor_26_out_5, full_subtractor_27_out_5,
       full_subtractor_28_out_5, full_subtractor_29_out_5, full_subtractor_30_out_5, full_subtractor_31_out_5;

  Full_Subtractor full_subtractor_1 (
    .A(A[24]), .B(B[24]), .in_1(1'b0), .out_4(Result[24]), .out_5(full_subtractor_1_out_5));
  Full_Subtractor full_subtractor_2 (
    .A(A[25]), .B(B[25]), .in_1(full_subtractor_1_out_5), .out_4(Result[25]), .out_5(full_subtractor_2_out_5));
  Full_Subtractor full_subtractor_3 (
    .A(A[26]), .B(B[26]), .in_1(full_subtractor_2_out_5), .out_4(Result[26]), .out_5(full_subtractor_3_out_5));
  Full_Subtractor full_subtractor_4 (
    .A(A[27]), .B(B[27]), .in_1(full_subtractor_3_out_5), .out_4(Result[27]), .out_5(full_subtractor_4_out_5));
  Full_Subtractor full_subtractor_5 (
    .A(A[28]), .B(B[28]), .in_1(full_subtractor_4_out_5), .out_4(Result[28]), .out_5(full_subtractor_5_out_5));
  Full_Subtractor full_subtractor_6 (
    .A(A[29]), .B(B[29]), .in_1(full_subtractor_5_out_5), .out_4(Result[29]), .out_5(full_subtractor_6_out_5));
  Full_Subtractor full_subtractor_7 (
    .A(A[30]), .B(B[30]), .in_1(full_subtractor_6_out_5), .out_4(Result[30]), .out_5(full_subtractor_7_out_5));
  Full_Subtractor full_subtractor_8 (
    .A(A[31]), .B(B[31]), .in_1(full_subtractor_7_out_5), .out_4(Result[31]), .out_5(full_subtractor_8_out_5));
  Full_Subtractor full_subtractor_9 (
    .A(A[16]), .B(B[16]), .in_1(full_subtractor_8_out_5), .out_4(Result[16]), .out_5(full_subtractor_9_out_5));
  Full_Subtractor full_subtractor_10 (
    .A(A[17]), .B(B[17]), .in_1(full_subtractor_9_out_5), .out_4(Result[17]), .out_5(full_subtractor_10_out_5));
  Full_Subtractor full_subtractor_11 (
    .A(A[18]), .B(B[18]), .in_1(full_subtractor_10_out_5), .out_4(Result[18]),
    .out_5(full_subtractor_11_out_5));
  Full_Subtractor full_subtractor_12 (
    .A(A[19]), .B(B[19]), .in_1(full_subtractor_11_out_5), .out_4(Result[19]),
    .out_5(full_subtractor_12_out_5));
  Full_Subtractor full_subtractor_13 (
    .A(A[20]), .B(B[20]), .in_1(full_subtractor_12_out_5), .out_4(Result[20]),
    .out_5(full_subtractor_13_out_5));
  Full_Subtractor full_subtractor_14 (
    .A(A[21]), .B(B[21]), .in_1(full_subtractor_13_out_5), .out_4(Result[21]),
    .out_5(full_subtractor_14_out_5));
  Full_Subtractor full_subtractor_15 (
    .A(A[22]), .B(B[22]), .in_1(full_subtractor_14_out_5), .out_4(Result[22]),
    .out_5(full_subtractor_15_out_5));
  Full_Subtractor full_subtractor_16 (
    .A(A[23]), .B(B[23]), .in_1(full_subtractor_15_out_5), .out_4(Result[23]),
    .out_5(full_subtractor_16_out_5));
  Full_Subtractor full_subtractor_17 (
    .A(A[8]), .B(B[8]), .in_1(full_subtractor_16_out_5), .out_4(Result[8]), .out_5(full_subtractor_17_out_5));
  Full_Subtractor full_subtractor_18 (
    .A(A[9]), .B(B[9]), .in_1(full_subtractor_17_out_5), .out_4(Result[9]), .out_5(full_subtractor_18_out_5));
  Full_Subtractor full_subtractor_19 (
    .A(A[10]), .B(B[10]), .in_1(full_subtractor_18_out_5), .out_4(Result[10]),
    .out_5(full_subtractor_19_out_5));
  Full_Subtractor full_subtractor_20 (
    .A(A[11]), .B(B[11]), .in_1(full_subtractor_19_out_5), .out_4(Result[11]),
    .out_5(full_subtractor_20_out_5));
  Full_Subtractor full_subtractor_21 (
    .A(A[12]), .B(B[12]), .in_1(full_subtractor_20_out_5), .out_4(Result[12]),
    .out_5(full_subtractor_21_out_5));
  Full_Subtractor full_subtractor_22 (
    .A(A[13]), .B(B[13]), .in_1(full_subtractor_21_out_5), .out_4(Result[13]),
    .out_5(full_subtractor_22_out_5));
  Full_Subtractor full_subtractor_23 (
    .A(A[14]), .B(B[14]), .in_1(full_subtractor_22_out_5), .out_4(Result[14]),
    .out_5(full_subtractor_23_out_5));
  Full_Subtractor full_subtractor_24 (
    .A(A[15]), .B(B[15]), .in_1(full_subtractor_23_out_5), .out_4(Result[15]),
    .out_5(full_subtractor_24_out_5));
  Full_Subtractor full_subtractor_25 (
    .A(A[0]), .B(B[0]), .in_1(full_subtractor_24_out_5), .out_4(Result[0]), .out_5(full_subtractor_25_out_5));
  Full_Subtractor full_subtractor_26 (
    .A(A[1]), .B(B[1]), .in_1(full_subtractor_25_out_5), .out_4(Result[1]), .out_5(full_subtractor_26_out_5));
  Full_Subtractor full_subtractor_27 (
    .A(A[2]), .B(B[2]), .in_1(full_subtractor_26_out_5), .out_4(Result[2]), .out_5(full_subtractor_27_out_5));
  Full_Subtractor full_subtractor_28 (
    .A(A[3]), .B(B[3]), .in_1(full_subtractor_27_out_5), .out_4(Result[3]), .out_5(full_subtractor_28_out_5));
  Full_Subtractor full_subtractor_29 (
    .A(A[4]), .B(B[4]), .in_1(full_subtractor_28_out_5), .out_4(Result[4]), .out_5(full_subtractor_29_out_5));
  Full_Subtractor full_subtractor_30 (
    .A(A[5]), .B(B[5]), .in_1(full_subtractor_29_out_5), .out_4(Result[5]), .out_5(full_subtractor_30_out_5));
  Full_Subtractor full_subtractor_31 (
    .A(A[6]), .B(B[6]), .in_1(full_subtractor_30_out_5), .out_4(Result[6]), .out_5(full_subtractor_31_out_5));
  Full_Subtractor full_subtractor_32 (
    .A(A[7]), .B(B[7]), .in_1(full_subtractor_31_out_5), .out_4(Result[7]));  // open: out_5
endmodule

module bitwise_AND (
  input  [31:0] A,
  input  [31:0] B,
  output [31:0] Result
);

  and and_1 (Result[24], A[24], B[24]);
  and and_2 (Result[25], A[25], B[25]);
  and and_3 (Result[26], A[26], B[26]);
  and and_4 (Result[27], A[27], B[27]);
  and and_5 (Result[28], A[28], B[28]);
  and and_6 (Result[29], A[29], B[29]);
  and and_7 (Result[30], A[30], B[30]);
  and and_8 (Result[31], A[31], B[31]);
  and and_9 (Result[16], A[16], B[16]);
  and and_10 (Result[17], A[17], B[17]);
  and and_11 (Result[18], A[18], B[18]);
  and and_12 (Result[19], A[19], B[19]);
  and and_13 (Result[20], A[20], B[20]);
  and and_14 (Result[21], A[21], B[21]);
  and and_15 (Result[22], A[22], B[22]);
  and and_16 (Result[23], A[23], B[23]);
  and and_17 (Result[8], A[8], B[8]);
  and and_18 (Result[9], A[9], B[9]);
  and and_19 (Result[10], A[10], B[10]);
  and and_20 (Result[11], A[11], B[11]);
  and and_21 (Result[12], A[12], B[12]);
  and and_22 (Result[13], A[13], B[13]);
  and and_23 (Result[14], A[14], B[14]);
  and and_24 (Result[15], A[15], B[15]);
  and and_25 (Result[0], A[0], B[0]);
  and and_26 (Result[1], A[1], B[1]);
  and and_27 (Result[2], A[2], B[2]);
  and and_28 (Result[3], A[3], B[3]);
  and and_29 (Result[4], A[4], B[4]);
  buf and_30 (Result[5], A[5]);  // AND_Gate
  buf and_31 (Result[6], A[6]);  // AND_Gate
  and and_32 (Result[7], A[7], B[7]);
endmodule

module bitwise_OR (
  input  [31:0] A,
  input  [31:0] B,
  output [31:0] Result
);

  or or_1 (Result[24], A[24], B[24]);
  or or_2 (Result[25], A[25], B[25]);
  or or_3 (Result[26], A[26], B[26]);
  or or_4 (Result[27], A[27], B[27]);
  or or_5 (Result[28], A[28], B[28]);
  or or_6 (Result[29], A[29], B[29]);
  or or_7 (Result[30], A[30], B[30]);
  or or_8 (Result[31], A[31], B[31]);
  or or_9 (Result[16], A[16], B[16]);
  or or_10 (Result[17], A[17], B[17]);
  or or_11 (Result[18], A[18], B[18]);
  or or_12 (Result[19], A[19], B[19]);
  or or_13 (Result[20], A[20], B[20]);
  or or_14 (Result[21], A[21], B[21]);
  or or_15 (Result[22], A[22], B[22]);
  or or_16 (Result[23], A[23], B[23]);
  or or_17 (Result[8], A[8], B[8]);
  or or_18 (Result[9], A[9], B[9]);
  or or_19 (Result[10], A[10], B[10]);
  or or_20 (Result[11], A[11], B[11]);
  or or_21 (Result[12], A[12], B[12]);
  or or_22 (Result[13], A[13], B[13]);
  or or_23 (Result[14], A[14], B[14]);
  or or_24 (Result[15], A[15], B[15]);
  or or_25 (Result[0], A[0], B[0]);
  or or_26 (Result[1], A[1], B[1]);
  or or_27 (Result[2], A[2], B[2]);
  or or_28 (Result[3], A[3], B[3]);
  or or_29 (Result[4], A[4], B[4]);
  or or_30 (Result[5], A[5], B[5]);
  or or_31 (Result[6], A[6], B[6]);
  or or_32 (Result[7], A[7], B[7]);
endmodule

module Bitwise_XOR (
  input  [31:0] A,
  input  [31:0] B,
  output [31:0] Result
);

  xor xor_1 (Result[24], A[24], B[24]);
  xor xor_2 (Result[25], A[25], B[25]);
  xor xor_3 (Result[26], A[26], B[26]);
  xor xor_4 (Result[27], A[27], B[27]);
  xor xor_5 (Result[28], A[28], B[28]);
  xor xor_6 (Result[29], A[29], B[29]);
  xor xor_7 (Result[30], A[30], B[30]);
  xor xor_8 (Result[31], A[31], B[31]);
  xor xor_9 (Result[16], A[16], B[16]);
  xor xor_10 (Result[17], A[17], B[17]);
  xor xor_11 (Result[18], A[18], B[18]);
  xor xor_12 (Result[19], A[19], B[19]);
  xor xor_13 (Result[20], A[20], B[20]);
  xor xor_14 (Result[21], A[21], B[21]);
  xor xor_15 (Result[22], A[22], B[22]);
  xor xor_16 (Result[23], A[23], B[23]);
  xor xor_17 (Result[8], A[8], B[8]);
  xor xor_18 (Result[9], A[9], B[9]);
  xor xor_19 (Result[10], A[10], B[10]);
  xor xor_20 (Result[11], A[11], B[11]);
  xor xor_21 (Result[12], A[12], B[12]);
  xor xor_22 (Result[13], A[13], B[13]);
  xor xor_23 (Result[14], A[14], B[14]);
  xor xor_24 (Result[15], A[15], B[15]);
  xor xor_25 (Result[0], A[0], B[0]);
  xor xor_26 (Result[1], A[1], B[1]);
  xor xor_27 (Result[2], A[2], B[2]);
  xor xor_28 (Result[3], A[3], B[3]);
  xor xor_29 (Result[4], A[4], B[4]);
  xor xor_30 (Result[5], A[5], B[5]);
  xor xor_31 (Result[6], A[6], B[6]);
  xor xor_32 (Result[7], A[7], B[7]);
endmodule

module Bitwise_not (
  input  [31:0] in_1,
  output [31:0] Result
);

  not not_1 (Result[0], in_1[0]);
  not not_2 (Result[1], in_1[1]);
  not not_3 (Result[2], in_1[2]);
  not not_4 (Result[3], in_1[3]);
  not not_5 (Result[4], in_1[4]);
  not not_6 (Result[5], in_1[5]);
  not not_7 (Result[6], in_1[6]);
  not not_8 (Result[7], in_1[7]);
  not not_9 (Result[8], in_1[8]);
  not not_10 (Result[9], in_1[9]);
  not not_11 (Result[10], in_1[10]);
  not not_12 (Result[11], in_1[11]);
  not not_13 (Result[12], in_1[12]);
  not not_14 (Result[13], in_1[13]);
  not not_15 (Result[14], in_1[14]);
  not not_16 (Result[15], in_1[15]);
  not not_17 (Result[16], in_1[16]);
  not not_18 (Result[17], in_1[17]);
  not not_19 (Result[18], in_1[18]);
  not not_20 (Result[19], in_1[19]);
  not not_21 (Result[20], in_1[20]);
  not not_22 (Result[21], in_1[21]);
  not not_23 (Result[22], in_1[22]);
  not not_24 (Result[23], in_1[23]);
  not not_25 (Result[24], in_1[24]);
  not not_26 (Result[25], in_1[25]);
  not not_27 (Result[26], in_1[26]);
  not not_28 (Result[27], in_1[27]);
  not not_29 (Result[28], in_1[28]);
  not not_30 (Result[29], in_1[29]);
  not not_31 (Result[30], in_1[30]);
  not not_32 (Result[31], in_1[31]);
endmodule

module left_shift (
  input  [31:0] A,
  input  in_2,
  output [31:0] Result
);

  wire and_1_out, and_3_out, and_4_out, and_5_out, and_6_out, and_7_out, and_8_out, and_9_out, and_10_out,
       and_11_out, and_12_out, and_13_out, and_14_out, and_15_out, and_16_out, and_17_out, and_18_out,
       and_19_out, and_20_out, and_21_out, and_22_out, and_23_out, and_24_out, and_25_out, and_26_out,
       and_27_out, and_28_out, and_29_out, and_30_out, and_31_out, and_32_out, and_33_out, and_34_out,
       and_35_out, and_36_out, and_37_out, and_38_out, and_39_out, and_40_out, and_41_out, and_42_out,
       and_43_out, and_44_out, and_45_out, and_46_out, and_47_out, and_48_out, and_49_out, and_50_out,
       and_51_out, and_52_out, and_53_out, and_54_out, and_55_out, and_56_out, and_57_out, and_58_out,
       and_59_out, and_60_out, and_62_out, not_1_out;

  not not_1 (not_1_out, in_2);
  and and_1 (and_1_out, A[0], A[0], in_2);
  and and_2 (Result[0], not_1_out, A[1]);
  and and_3 (and_3_out, A[1], in_2);
  and and_4 (and_4_out, not_1_out, A[2]);
  and and_5 (and_5_out, A[2], in_2);
  and and_6 (and_6_out, not_1_out, A[3]);
  and and_7 (and_7_out, A[3], in_2);
  and and_8 (and_8_out, not_1_out, A[4]);
  and and_9 (and_9_out, A[4], in_2);
  and and_10 (and_10_out, not_1_out, A[5]);
  and and_11 (and_11_out, A[5], in_2);
  and and_12 (and_12_out, not_1_out, A[6]);
  and and_13 (and_13_out, A[6], in_2);
  and and_14 (and_14_out, not_1_out, A[7]);
  and and_15 (and_15_out, A[7], in_2);
  and and_16 (and_16_out, not_1_out, A[8]);
  and and_17 (and_17_out, A[8], A[8], in_2);
  and and_18 (and_18_out, not_1_out, A[9]);
  and and_19 (and_19_out, A[9], in_2);
  and and_20 (and_20_out, not_1_out, A[10]);
  and and_21 (and_21_out, A[10], in_2);
  and and_22 (and_22_out, not_1_out, A[11]);
  and and_23 (and_23_out, A[11], in_2);
  and and_24 (and_24_out, not_1_out, A[12]);
  and and_25 (and_25_out, A[12], in_2);
  and and_26 (and_26_out, not_1_out, A[13]);
  and and_27 (and_27_out, A[13], in_2);
  and and_28 (and_28_out, not_1_out, A[14]);
  and and_29 (and_29_out, A[14], in_2);
  and and_30 (and_30_out, not_1_out, A[15]);
  and and_31 (and_31_out, A[15], in_2);
  and and_32 (and_32_out, not_1_out, A[16]);
  and and_33 (and_33_out, A[16], in_2);
  and and_34 (and_34_out, not_1_out, A[17]);
  and and_35 (and_35_out, A[17], in_2);
  and and_36 (and_36_out, not_1_out, A[18]);
  and and_37 (and_37_out, A[18], in_2);
  and and_38 (and_38_out, not_1_out, A[19]);
  and and_39 (and_39_out, A[19], in_2);
  and and_40 (and_40_out, not_1_out, A[20]);
  and and_41 (and_41_out, A[20], in_2);
  and and_42 (and_42_out, not_1_out, A[21]);
  and and_43 (and_43_out, A[21], in_2);
  and and_44 (and_44_out, not_1_out, A[22]);
  and and_45 (and_45_out, A[22], in_2);
  and and_46 (and_46_out, not_1_out, A[23]);
  and and_47 (and_47_out, A[23], in_2);
  and and_48 (and_48_out, not_1_out, A[24]);
  and and_49 (and_49_out, A[24], in_2);
  and and_50 (and_50_out, not_1_out, A[25]);
  and and_51 (and_51_out, A[25], in_2);
  and and_52 (and_52_out, not_1_out, A[26]);
  and and_53 (and_53_out, A[26], in_2);
  and and_54 (and_54_out, not_1_out, A[27]);
  and and_55 (and_55_out, A[27], in_2);
  and and_56 (and_56_out, not_1_out, A[28]);
  and and_57 (and_57_out, A[28], in_2);
  and and_58 (and_58_out, not_1_out, A[29]);
  and and_59 (and_59_out, A[29], in_2);
  and and_60 (and_60_out, not_1_out, A[30]);
  and and_61 (Result[31], A[30], in_2);
  and and_62 (and_62_out, not_1_out, A[31]);
  or or_1 (Result[1], and_1_out, and_1_out, and_4_out, and_4_out);
  or or_2 (Result[5], and_9_out, and_12_out);
  or or_3 (Result[7], and_13_out, and_13_out, and_16_out, and_16_out);
  or or_4 (Result[9], and_17_out, and_20_out);
  or or_5 (Result[11], and_21_out, and_24_out);
  or or_6 (Result[13], and_25_out, and_28_out);
  or or_7 (Result[15], and_29_out, and_32_out);
  or or_8 (Result[17], and_33_out, and_36_out);
  or or_9 (Result[19], and_37_out, and_40_out);
  or or_10 (Result[21], and_41_out, and_44_out);
  or or_11 (Result[23], and_45_out, and_48_out);
  or or_12 (Result[25], and_49_out, and_52_out);
  or or_13 (Result[27], and_53_out, and_56_out);
  or or_14 (Result[29], and_57_out, and_60_out);
  or or_15 (Result[3], and_5_out, and_8_out);
  or or_16 (Result[18], and_35_out, and_38_out);
  or or_17 (Result[20], and_39_out, and_42_out);
  or or_18 (Result[22], and_43_out, and_46_out);
  or or_19 (Result[24], and_47_out, and_50_out);
  or or_20 (Result[26], and_51_out, and_54_out);
  or or_21 (Result[28], and_55_out, and_58_out);
  or or_22 (Result[30], and_59_out, and_62_out);
  or or_23 (Result[4], and_7_out, and_10_out);
  or or_24 (Result[6], and_11_out, and_14_out);
  or or_25 (Result[8], and_15_out, and_18_out);
  or or_26 (Result[10], and_19_out, and_22_out);
  or or_27 (Result[12], and_23_out, and_26_out);
  or or_28 (Result[14], and_27_out, and_30_out);
  or or_29 (Result[16], and_31_out, and_34_out);
  or or_30 (Result[2], and_3_out, and_6_out, and_6_out);
endmodule

module Full_Adder (
  input  in_1,
  input  in_2,
  input  in_3,
  output out_4,
  output out_5
);

  wire and_1_out, and_2_out, xor_1_out;

  xor xor_1 (xor_1_out, in_1, in_2);
  xor xor_2 (out_4, xor_1_out, in_3);
  and and_1 (and_1_out, xor_1_out, in_3, in_3);
  and and_2 (and_2_out, in_1, in_2);
  or or_1 (out_5, and_1_out, and_2_out);
endmodule

module Full_Subtractor (
  input  in_1,
  input  A,
  input  B,
  output out_4,
  output out_5
);

  wire and_1_out, and_2_out, not_1_out, not_2_out, xor_1_out;

  not not_1 (not_1_out, A);
  xor xor_1 (xor_1_out, A, B);
  and and_1 (and_1_out, B, not_1_out);
  not not_2 (not_2_out, xor_1_out);
  and and_2 (and_2_out, not_2_out, in_1);
  xor xor_2 (out_4, in_1, xor_1_out);
  or or_1 (out_5, and_2_out, and_1_out);
endmodule
