// Logisim project CPU RISC V.circ as structural Verilog: 2 circuits, main circuit main
module main (
  input  [6:0] in_1,
  input  [2:0] in_2,
  output [1:0] out_3,
  output [1:0] out_4,
  output [31:0] out_5,
  output [5:0] out_6,
  output [31:0] out_7,
  output [31:0] out_8,
  output [31:0] out_9
);

  wire and_1_out, CLK, comparator_1_eq, comparator_2_eq, comparator_3_eq, comparator_4_eq, comparator_5_eq,
       comparator_6_lt, comparator_7_eq, comparator_8_eq, comparator_9_eq, comparator_10_eq,
       comparator_11_eq, comparator_12_eq, comparator_13_eq, comparator_14_eq, comparator_15_eq,
       multiplexer_10_out, Reset;
  wire [0:0] rom_1_data_6;
  wire [2:0] multiplexer_2_out, multiplexer_3_out, multiplexer_4_out, multiplexer_5_out, multiplexer_6_out,
       multiplexer_12_out, multiplexer_13_out, multiplexer_14_out, multiplexer_15_out, multiplexer_16_out,
       multiplexer_17_out, multiplexer_18_out, multiplexer_19_out, multiplexer_21_out, or_1_out, or_2_out,
       or_3_out, rom_1_data_2;
  wire [4:0] rom_1_data_3, rom_1_data_4, rom_1_data_5;
  wire [6:0] rom_1_data;
  wire [8:2] multiplexer_8_out;
  wire [31:0] adder_1_out, adder_2_out, adder_3_out, and_2_out, bit_extender_1_out, bit_extender_2_out,
       bit_extender_3_out, bit_extender_4_out, multiplexer_1_out, multiplexer_7_out, ram_1_data,
       register_1_q, register_32bit_1_read_data_2, subtractor_1_out;

  // Probe on adder_1_out
  Adder #(.width(32)) adder_1 (
    .a(32'h4), .b({register_1_q[31:8], out_6, register_1_q[1:0]}), .out(adder_1_out));  // open: cin, cout
  Adder #(.width(32)) adder_2 (
    .a(bit_extender_3_out), .b({register_1_q[31:8], out_6, register_1_q[1:0]}), .out(adder_2_out));  // open: cin, cout
  // Probe on adder_2_out
  Multiplexer #(.width(32), .enable("false")) multiplexer_1 (
    .in0(adder_1_out), .in1(adder_2_out), .out(multiplexer_1_out), .sel(and_1_out));
  Clock clock_1 (.out(CLK));
  Button button_1 (.out(Reset));
  // Probe on bit_extender_3_out
  Register #(.width(32)) register_1 (
    .D(multiplexer_1_out), .Q({register_1_q[31:8], out_6, register_1_q[1:0]}), .clk(CLK), .clr(Reset));  // open: en
  // Probe on {in_1, rom_1_data_4, rom_1_data_3, rom_1_data_2, rom_1_data_5, rom_1_data[6], rom_1_data_6[0], rom_1_data[4:0]}
  Comparator #(.width(7)) comparator_1 (
    .a({rom_1_data[6], rom_1_data_6[0], rom_1_data[4:0]}), .b(7'b0000011), .eq(comparator_1_eq));  // open: gt, lt
  Comparator #(.width(7)) comparator_2 (
    .a({rom_1_data[6], rom_1_data_6[0], rom_1_data[4:0]}), .b(7'b0100011), .eq(comparator_2_eq));  // open: gt, lt
  Comparator #(.width(7)) comparator_3 (
    .a({rom_1_data[6], rom_1_data_6[0], rom_1_data[4:0]}), .b(7'b0110011), .eq(comparator_3_eq));  // open: gt, lt
  Comparator #(.width(7)) comparator_4 (
    .a({rom_1_data[6], rom_1_data_6[0], rom_1_data[4:0]}), .b(7'b1100011), .eq(comparator_4_eq));  // open: gt, lt
  Comparator #(.width(7)) comparator_5 (
    .a({rom_1_data[6], rom_1_data_6[0], rom_1_data[4:0]}), .b(7'b0010011), .eq(comparator_5_eq));  // open: gt, lt
  assign bit_extender_1_out = {{20{1'b0}}, {in_1, rom_1_data_4}};  // Bit_Extender bit_extender_1
  assign bit_extender_2_out = {{20{1'b0}}, {in_1, rom_1_data_5}};  // Bit_Extender bit_extender_2
  assign bit_extender_3_out = {{19{1'b0}}, {in_1[6], rom_1_data_5[0], in_1[5:0], rom_1_data_5[4:1], 1'b0}};  // Bit_Extender bit_extender_3
  ROM #(.addrWidth(24), .dataWidth(32)) rom_1 (
    .addr({register_1_q[25:8], out_6}),
    .data({in_1, rom_1_data_4, rom_1_data_3, rom_1_data_2, rom_1_data_5, rom_1_data[6], rom_1_data_6[0], rom_1_data[4:0]}));  // open: sel
  Multiplexer #(.width(3), .enable("false")) multiplexer_2 (
    .in0(3'b000), .in1(3'b001), .out(multiplexer_2_out), .sel(comparator_1_eq));
  Multiplexer #(.width(3), .enable("false")) multiplexer_3 (
    .in0(3'b000), .in1(3'b010), .out(multiplexer_3_out), .sel(comparator_2_eq));
  Multiplexer #(.width(3), .enable("false")) multiplexer_4 (
    .in0(3'b000), .in1(3'b011), .out(multiplexer_4_out), .sel(comparator_3_eq));
  Multiplexer #(.width(3), .enable("false")) multiplexer_5 (
    .in0(3'b000), .in1(3'b100), .out(multiplexer_5_out), .sel(comparator_4_eq));
  Multiplexer #(.width(3), .enable("false")) multiplexer_6 (
    .in0(3'b000), .in1(3'b101), .out(multiplexer_6_out), .sel(comparator_5_eq));
  Multiplexer #(.select(2), .width(32), .enable("false")) multiplexer_7 (
    .in0(bit_extender_1_out), .in1(bit_extender_2_out), .in2(bit_extender_3_out), .out(multiplexer_7_out),
    .sel(out_4));  // open: in3
  // Probe on rom_1_data_4
  // Probe on multiplexer_7_out
  assign or_1_out = multiplexer_2_out | multiplexer_3_out | multiplexer_4_out | multiplexer_5_out | multiplexer_6_out;  // OR_Gate or_1, 3 bits wide
  // Probe on {rom_1_data[6], rom_1_data_6[0], rom_1_data[4:0]}
  Multiplexer #(.select(3), .width(9), .enable("false")) multiplexer_8 (
    .in0({9{1'b0}}), .in1(9'h128), .in2(9'h70), .in3(9'h102), .in4(9'h35), .in5(9'h120), .in6({9{1'b0}}),
    .in7({9{1'b0}}), .out({multiplexer_8_out[8], out_4, multiplexer_8_out[5:2], out_3}), .sel(or_1_out));
  REGISTER_32bit register_32bit_1 (
    .Write_Register(rom_1_data_5), .Write_Data(out_5), .Read_Address_1(rom_1_data_3),
    .Read_Address_2(rom_1_data_4), .Write_Enable(multiplexer_8_out[8]), .CLK(CLK), .Read_Data_1(out_7),
    .Read_Data_2(register_32bit_1_read_data_2));
  Multiplexer #(.width(32), .enable("false")) multiplexer_9 (
    .in0(register_32bit_1_read_data_2), .in1(multiplexer_7_out), .out(out_8), .sel(multiplexer_10_out));
  and and_1 (and_1_out, multiplexer_8_out[2], comparator_15_eq);
  Multiplexer #(.enable("false")) multiplexer_10 (
    .in0(multiplexer_8_out[5]), .in1(1'b0), .out(multiplexer_10_out), .sel(multiplexer_8_out[2]));
  Adder #(.width(32)) adder_3 (.a(out_7), .b(out_8), .out(adder_3_out));  // open: cin, cout
  Subtractor #(.width(32)) subtractor_1 (.a(out_7), .b(out_8), .out(subtractor_1_out));  // open: bin, bout
  assign and_2_out = out_7 & out_8;  // AND_Gate and_2, 32 bits wide
  Comparator #(.width(32)) comparator_6 (.a(out_7), .b(out_8), .lt(comparator_6_lt));  // open: gt, eq
  assign bit_extender_4_out = {{31{1'b0}}, comparator_6_lt};  // Bit_Extender bit_extender_4
  // Probe on out_9
  Multiplexer #(.select(3), .width(32), .enable("false")) multiplexer_11 (
    .in0(adder_3_out), .in1(subtractor_1_out), .in5(and_2_out), .in7(bit_extender_4_out), .out(out_9),
    .sel(multiplexer_21_out));  // open: in2, in3, in4, in6
  // Probe on multiplexer_21_out
  Comparator #(.width(2)) comparator_7 (
    .a({in_1[5], rom_1_data_6[0]}), .b(2'b11), .eq(comparator_7_eq));  // open: gt, lt
  Comparator #(.width(3)) comparator_8 (.a(in_2), .b(3'b000), .eq(comparator_8_eq));  // open: gt, lt
  Comparator #(.width(3)) comparator_9 (.a(in_2), .b(3'b010), .eq(comparator_9_eq));  // open: gt, lt
  Comparator #(.width(3)) comparator_10 (.a(in_2), .b(3'b110), .eq(comparator_10_eq));  // open: gt, lt
  Comparator #(.width(3)) comparator_11 (.a(in_2), .b(3'b111), .eq(comparator_11_eq));  // open: gt, lt
  Comparator #(.width(2)) comparator_12 (.a(out_3), .b(2'b00), .eq(comparator_12_eq));  // open: gt, lt
  Comparator #(.width(2)) comparator_13 (.a(out_3), .b(2'b01), .eq(comparator_13_eq));  // open: gt, lt
  Comparator #(.width(2)) comparator_14 (.a(out_3), .b(2'b10), .eq(comparator_14_eq));  // open: gt, lt
  Comparator #(.width(32)) comparator_15 (.a(out_9), .b({32{1'b0}}), .eq(comparator_15_eq));  // open: gt, lt
  Multiplexer #(.width(3), .enable("false")) multiplexer_12 (
    .in0(3'b000), .in1(3'b001), .out(multiplexer_12_out), .sel(comparator_7_eq));
  Multiplexer #(.width(3), .enable("false")) multiplexer_13 (
    .in0(3'b000), .in1(3'b101), .out(multiplexer_13_out), .sel(comparator_9_eq));
  Multiplexer #(.width(3), .enable("false")) multiplexer_14 (
    .in0(3'b000), .in1(3'b011), .out(multiplexer_14_out), .sel(comparator_10_eq));
  Multiplexer #(.width(3), .enable("false")) multiplexer_15 (
    .in0(3'b000), .in1(3'b010), .out(multiplexer_15_out), .sel(comparator_11_eq));
  Multiplexer #(.width(3), .enable("false")) multiplexer_16 (
    .in0(3'b000), .in1(3'b000), .out(multiplexer_16_out), .sel(comparator_12_eq));
  Multiplexer #(.width(3), .enable("false")) multiplexer_17 (
    .in0(3'b000), .in1(3'b001), .out(multiplexer_17_out), .sel(comparator_13_eq));
  Multiplexer #(.width(3), .enable("false")) multiplexer_18 (
    .in0(3'b000), .in1(3'b010), .out(multiplexer_18_out), .sel(comparator_14_eq));
  Multiplexer #(.width(3), .enable("false")) multiplexer_19 (
    .in0(3'b000), .in1(multiplexer_12_out), .out(multiplexer_19_out), .sel(comparator_8_eq));
  Multiplexer #(.width(32), .enable("false")) multiplexer_20 (
    .in0(out_9), .in1(ram_1_data), .out(out_5), .sel(multiplexer_8_out[3]));
  assign or_2_out = multiplexer_19_out | multiplexer_13_out | multiplexer_14_out | multiplexer_15_out;  // OR_Gate or_2, 3 bits wide
  assign or_3_out = multiplexer_16_out | multiplexer_17_out | multiplexer_18_out;  // OR_Gate or_3, 3 bits wide
  Multiplexer #(.select(3), .width(3), .enable("false")) multiplexer_21 (
    .in0(3'b000), .in1(3'b001), .in2(or_2_out), .out(multiplexer_21_out), .sel(or_3_out));  // open: in3, in4, in5, in6, in7
  // Probe on or_3_out
  RAM #(.addrWidth(24), .dataWidth(32), .bus("separate")) ram_1 (
    .addr(out_9[23:0]), .din(register_32bit_1_read_data_2), .data(ram_1_data), .str(multiplexer_8_out[4]),
    .clk(CLK));  // open: sel, ld, clr

  // Notes on the sheet:
  //   INSTRUCITON FETCH STAGE: PC and ROM
  //   IMMEDIATE GENERATOR
  //   CONTROL UNIT 
  //   contents of rom_1 (hex, n*v repeats v):
  //   0 700313 628463 6283b3 520333
  //   alu src
  //   EXECUTION STAGE 
  //   WRITEBACK
  //   ALU CONTROL
  //   MEMORY ACCESS STAGE
endmodule

module REGISTER_32bit (
  input  [4:0] Write_Register,
  input  [31:0] Write_Data,
  input  [4:0] Read_Address_1,
  input  [4:0] Read_Address_2,
  input  Write_Enable,
  input  CLK,
  output [31:0] Read_Data_1,
  output [31:0] Read_Data_2
);

  wire and_1_out, and_2_out, and_3_out, and_4_out, and_5_out, and_6_out, and_7_out, and_8_out, and_9_out,
       and_10_out, and_11_out, and_12_out, and_13_out, and_14_out, and_15_out, and_16_out, and_17_out,
       and_18_out, and_19_out, and_20_out, and_21_out, and_22_out, and_23_out, and_24_out, and_25_out,
       and_26_out, and_27_out, and_28_out, and_29_out, and_30_out, and_31_out, and_32_out, decoder_1_out0,
       decoder_1_out1, decoder_1_out2, decoder_1_out3, decoder_1_out4, decoder_1_out5, decoder_1_out6,
       decoder_1_out7, decoder_1_out8, decoder_1_out9, decoder_1_out10, decoder_1_out11, decoder_1_out12,
       decoder_1_out13, decoder_1_out14, decoder_1_out15, decoder_1_out16, decoder_1_out17, decoder_1_out18,
       decoder_1_out19, decoder_1_out20, decoder_1_out21, decoder_1_out22, decoder_1_out23, decoder_1_out24,
       decoder_1_out25, decoder_1_out26, decoder_1_out27, decoder_1_out28, decoder_1_out29, decoder_1_out30,
       decoder_1_out31;
  wire [31:0] register_1_q, register_2_q, register_3_q, register_4_q, register_5_q, register_6_q,
       register_7_q, register_8_q, register_9_q, register_10_q, register_11_q, register_12_q, register_13_q,
       register_14_q, register_15_q, register_16_q, register_17_q, register_18_q, register_19_q,
       register_20_q, register_21_q, register_22_q, register_23_q, register_24_q, register_25_q,
       register_26_q, register_27_q, register_28_q, register_29_q, register_30_q, register_31_q,
       register_32_q;

  Decoder #(.select(5)) decoder_1 (
    .out0(decoder_1_out0), .out1(decoder_1_out1), .out2(decoder_1_out2), .out3(decoder_1_out3),
    .out4(decoder_1_out4), .out5(decoder_1_out5), .out6(decoder_1_out6), .out7(decoder_1_out7),
    .out8(decoder_1_out8), .out9(decoder_1_out9), .out10(decoder_1_out10), .out11(decoder_1_out11),
    .out12(decoder_1_out12), .out13(decoder_1_out13), .out14(decoder_1_out14), .out15(decoder_1_out15),
    .out16(decoder_1_out16), .out17(decoder_1_out17), .out18(decoder_1_out18), .out19(decoder_1_out19),
    .out20(decoder_1_out20), .out21(decoder_1_out21), .out22(decoder_1_out22), .out23(decoder_1_out23),
    .out24(decoder_1_out24), .out25(decoder_1_out25), .out26(decoder_1_out26), .out27(decoder_1_out27),
    .out28(decoder_1_out28), .out29(decoder_1_out29), .out30(decoder_1_out30), .out31(decoder_1_out31),
    .sel(Write_Register));  // open: en
  and and_1 (and_1_out, decoder_1_out0, Write_Enable);
  and and_2 (and_2_out, decoder_1_out1, Write_Enable);
  and and_3 (and_3_out, decoder_1_out2, Write_Enable);
  and and_4 (and_4_out, decoder_1_out3, Write_Enable);
  and and_5 (and_5_out, decoder_1_out4, Write_Enable);
  and and_6 (and_6_out, decoder_1_out5, Write_Enable);
  and and_7 (and_7_out, decoder_1_out6, Write_Enable);
  and and_8 (and_8_out, decoder_1_out7, Write_Enable);
  Register #(.width(32)) register_1 (.D(Write_Data), .en(and_1_out), .Q(register_1_q), .clk(CLK), .clr(1'b1));
  Register #(.width(32)) register_2 (.D(Write_Data), .en(and_2_out), .Q(register_2_q), .clk(CLK));  // open: clr
  Register #(.width(32)) register_3 (.D(Write_Data), .en(and_3_out), .Q(register_3_q), .clk(CLK));  // open: clr
  Register #(.width(32)) register_4 (.D(Write_Data), .en(and_4_out), .Q(register_4_q), .clk(CLK));  // open: clr
  Register #(.width(32)) register_5 (.D(Write_Data), .en(and_5_out), .Q(register_5_q), .clk(CLK));  // open: clr
  Register #(.width(32)) register_6 (.D(Write_Data), .en(and_6_out), .Q(register_6_q), .clk(CLK));  // open: clr
  Register #(.width(32)) register_7 (.D(Write_Data), .en(and_7_out), .Q(register_7_q), .clk(CLK));  // open: clr
  Register #(.width(32)) register_8 (.D(Write_Data), .en(and_8_out), .Q(register_8_q), .clk(CLK));  // open: clr
  and and_9 (and_9_out, decoder_1_out8, Write_Enable);
  and and_10 (and_10_out, decoder_1_out9, Write_Enable);
  and and_11 (and_11_out, decoder_1_out10, Write_Enable);
  and and_12 (and_12_out, decoder_1_out11, Write_Enable);
  and and_13 (and_13_out, decoder_1_out12, Write_Enable);
  and and_14 (and_14_out, decoder_1_out13, Write_Enable);
  and and_15 (and_15_out, decoder_1_out14, Write_Enable);
  and and_16 (and_16_out, decoder_1_out15, Write_Enable);
  Register #(.width(32)) register_9 (.D(Write_Data), .en(and_9_out), .Q(register_9_q), .clk(CLK));  // open: clr
  Register #(.width(32)) register_10 (.D(Write_Data), .en(and_10_out), .Q(register_10_q), .clk(CLK));  // open: clr
  Register #(.width(32)) register_11 (.D(Write_Data), .en(and_11_out), .Q(register_11_q), .clk(CLK));  // open: clr
  Register #(.width(32)) register_12 (.D(Write_Data), .en(and_12_out), .Q(register_12_q), .clk(CLK));  // open: clr
  Register #(.width(32)) register_13 (.D(Write_Data), .en(and_13_out), .Q(register_13_q), .clk(CLK));  // open: clr
  Register #(.width(32)) register_14 (.D(Write_Data), .en(and_14_out), .Q(register_14_q), .clk(CLK));  // open: clr
  Register #(.width(32)) register_15 (.D(Write_Data), .en(and_15_out), .Q(register_15_q), .clk(CLK));  // open: clr
  Register #(.width(32)) register_16 (.D(Write_Data), .en(and_16_out), .Q(register_16_q), .clk(CLK));  // open: clr
  and and_17 (and_17_out, decoder_1_out16, Write_Enable);
  and and_18 (and_18_out, decoder_1_out17, Write_Enable);
  and and_19 (and_19_out, decoder_1_out18, Write_Enable);
  and and_20 (and_20_out, decoder_1_out19, Write_Enable);
  and and_21 (and_21_out, decoder_1_out20, Write_Enable);
  and and_22 (and_22_out, decoder_1_out21, Write_Enable);
  and and_23 (and_23_out, decoder_1_out22, Write_Enable);
  and and_24 (and_24_out, decoder_1_out23, Write_Enable);
  Register #(.width(32)) register_17 (.D(Write_Data), .en(and_17_out), .Q(register_17_q), .clk(CLK));  // open: clr
  Register #(.width(32)) register_18 (.D(Write_Data), .en(and_18_out), .Q(register_18_q), .clk(CLK));  // open: clr
  Register #(.width(32)) register_19 (.D(Write_Data), .en(and_19_out), .Q(register_19_q), .clk(CLK));  // open: clr
  Register #(.width(32)) register_20 (.D(Write_Data), .en(and_20_out), .Q(register_20_q), .clk(CLK));  // open: clr
  Register #(.width(32)) register_21 (.D(Write_Data), .en(and_21_out), .Q(register_21_q), .clk(CLK));  // open: clr
  Register #(.width(32)) register_22 (.D(Write_Data), .en(and_22_out), .Q(register_22_q), .clk(CLK));  // open: clr
  Register #(.width(32)) register_23 (.D(Write_Data), .en(and_23_out), .Q(register_23_q), .clk(CLK));  // open: clr
  Register #(.width(32)) register_24 (.D(Write_Data), .en(and_24_out), .Q(register_24_q), .clk(CLK));  // open: clr
  and and_25 (and_25_out, decoder_1_out24, Write_Enable);
  and and_26 (and_26_out, decoder_1_out25, Write_Enable);
  and and_27 (and_27_out, decoder_1_out26, Write_Enable);
  and and_28 (and_28_out, decoder_1_out27, Write_Enable);
  and and_29 (and_29_out, decoder_1_out28, Write_Enable);
  and and_30 (and_30_out, decoder_1_out29, Write_Enable);
  and and_31 (and_31_out, decoder_1_out30, Write_Enable);
  and and_32 (and_32_out, decoder_1_out31, Write_Enable);
  Register #(.width(32)) register_25 (.D(Write_Data), .en(and_25_out), .Q(register_25_q), .clk(CLK));  // open: clr
  Register #(.width(32)) register_26 (.D(Write_Data), .en(and_26_out), .Q(register_26_q), .clk(CLK));  // open: clr
  Register #(.width(32)) register_27 (.D(Write_Data), .en(and_27_out), .Q(register_27_q), .clk(CLK));  // open: clr
  Register #(.width(32)) register_28 (.D(Write_Data), .en(and_28_out), .Q(register_28_q), .clk(CLK));  // open: clr
  Register #(.width(32)) register_29 (.D(Write_Data), .en(and_29_out), .Q(register_29_q), .clk(CLK));  // open: clr
  Register #(.width(32)) register_30 (.D(Write_Data), .en(and_30_out), .Q(register_30_q), .clk(CLK));  // open: clr
  Register #(.width(32)) register_31 (.D(Write_Data), .en(and_31_out), .Q(register_31_q), .clk(CLK));  // open: clr
  Register #(.width(32)) register_32 (.D(Write_Data), .en(and_32_out), .Q(register_32_q), .clk(CLK));  // open: clr
  Multiplexer #(.select(5), .width(32)) multiplexer_1 (
    .in0(register_1_q), .in1(register_2_q), .in2(register_3_q), .in3(register_4_q), .in4(register_5_q),
    .in5(register_6_q), .in6(register_7_q), .in7(register_8_q), .in8(register_9_q), .in9(register_10_q),
    .in10(register_11_q), .in11(register_12_q), .in12(register_13_q), .in13(register_14_q),
    .in14(register_15_q), .in15(register_16_q), .in16(register_17_q), .in17(register_18_q),
    .in18(register_19_q), .in19(register_20_q), .in20(register_21_q), .in21(register_22_q),
    .in22(register_23_q), .in23(register_24_q), .in24(register_25_q), .in25(register_26_q),
    .in26(register_27_q), .in27(register_28_q), .in28(register_29_q), .in29(register_30_q),
    .in30(register_31_q), .in31(register_32_q), .out(Read_Data_1), .sel(Read_Address_1));  // open: en
  Multiplexer #(.select(5), .width(32)) multiplexer_2 (
    .in0(register_1_q), .in1(register_2_q), .in2(register_3_q), .in3(register_4_q), .in4(register_5_q),
    .in5(register_6_q), .in6(register_7_q), .in7(register_8_q), .in8(register_9_q), .in9(register_10_q),
    .in10(register_11_q), .in11(register_12_q), .in12(register_13_q), .in13(register_14_q),
    .in14(register_15_q), .in15(register_16_q), .in16(register_17_q), .in17(register_18_q),
    .in18(register_19_q), .in19(register_20_q), .in20(register_21_q), .in21(register_22_q),
    .in22(register_23_q), .in23(register_24_q), .in24(register_25_q), .in25(register_26_q),
    .in26(register_27_q), .in27(register_28_q), .in28(register_29_q), .in29(register_30_q),
    .in30(register_31_q), .in31(register_32_q), .out(Read_Data_2), .sel(Read_Address_2));  // open: en

  // Notes on the sheet:
  //   Zero Register
endmodule
